# Fritzing sketch InternetWeatheraAndClock (saved by Fritzing 0.9.3b)

parts:
  ESP_12-_E_Module_(NodeMCU) = Gizwits WiFi Witty ESP-12F
  0_96_Inch_OLED_display = Grove OLED 128x96

nets:
  VCC: ESP_12-_E_Module_(NodeMCU).VCC, 0_96_Inch_OLED_display.VCC
  GND: ESP_12-_E_Module_(NodeMCU).GND, 0_96_Inch_OLED_display.GND
  N1: ESP_12-_E_Module_(NodeMCU).GPIO4, 0_96_Inch_OLED_display.SCL
  N2: ESP_12-_E_Module_(NodeMCU).GPIO5, 0_96_Inch_OLED_display.SDA
